# Fritzing sketch sensorAparcamiento (saved by Fritzing 0.9.3b)
breadboards: 1

parts:
  Componente1 = Arduino Uno (Rev3)
  Componente2 = LED Matrix - Serial Interface - Red/Green/Blue
  hc-sr1 = hc-sr04
  J1 = Piezo Speaker

nets:
  N1: Componente1.D10_PWM/SS, Componente2.MOSI
  N2: Componente1.D11_PWM/MOSI, Componente2.GND
  N3: Componente1.D12/MISO, Componente2.CS
  GND: Componente1.GND, Componente2.SCK, hc-sr1.GND
  N4: Componente1.D2, J1.pin2
  N5: Componente1.D3_PWM, hc-sr1.Trig
  N6: Componente1.D4, hc-sr1.Echo
  VCC: Componente1.5V, Componente2.VCC, hc-sr1.VCC
